// Logisim project SAP.circ as structural Verilog: 5 circuits, main circuit main
module main (
);

  wire and_1_out, clock_1_out, decoder_1_out0, decoder_1_out1, decoder_1_out2, decoder_1_out3,
       decoder_1_out4, decoder_1_out5, decoder_1_out6, decoder_1_out7, not_1_out, not_2_out, RESET_out;
  wire [3:0] binary_to_bcd_converter_1_p3, binary_to_bcd_converter_1_p4, binary_to_bcd_converter_1_p5,
       eightbitregister_2_output_direct, programcounter_1_out_to_bus;
  wire [7:0] controlled_buffer_1_out, controlled_buffer_2_out, controlled_buffer_4_out,
       controlled_buffer_5_out, controlled_buffer_6_out, eightbitregister_1_output_data,
       eightbitregister_1_output_direct, eightbitregister_3_output_direct, eightbitregister_4_output_direct,
       eightbitregister_5_output_direct, ram_1_dout;
  wire [7:4] programcounter_1_out_to_bus_2;
  wire [7:7] eightbitregister_2_output_direct_2;
  wire [31:0] EEPROM_data;

  LedBar #(.matrixcols(4)) ledbar_1 (
    .led0(programcounter_1_out_to_bus[3]), .led1(programcounter_1_out_to_bus[2]),
    .led2(programcounter_1_out_to_bus[1]), .led3(programcounter_1_out_to_bus[0]));
  ROM #(.dataWidth(32)) EEPROM (
    .addr({eightbitregister_1_output_direct[7:4], 1'b0, programcounter_1_out_to_bus[2:0]}), .data(EEPROM_data));
  LedBar ledbar_2 (
    .led0(decoder_1_out0), .led1(decoder_1_out1), .led2(decoder_1_out2), .led3(decoder_1_out3),
    .led4(decoder_1_out4), .led5(decoder_1_out5), .led6(decoder_1_out6), .led7(decoder_1_out7));
  Clock clock_1 (.out(clock_1_out));
  Decoder #(.select(3)) decoder_1 (
    .out0(decoder_1_out0), .out1(decoder_1_out1), .out2(decoder_1_out2), .out3(decoder_1_out3),
    .out4(decoder_1_out4), .out5(decoder_1_out5), .out6(decoder_1_out6), .out7(decoder_1_out7),
    .sel(programcounter_1_out_to_bus[2:0]), .en(1'b1));
  not not_1 (not_1_out, EEPROM_data[14]);
  and and_1 (and_1_out, not_1_out, clock_1_out);
  not not_2 (not_2_out, and_1_out);
  ProgramCounter programcounter_1 (
    .OUT_ENABLE(1'b1), .LOAD_ENABLE(1'b0), .CLR(decoder_1_out7), .cin(1'b1), .enable(1'b1), .CLK(not_2_out),
    .out_to_bus({programcounter_1_out_to_bus_2, programcounter_1_out_to_bus}));  // open: COUNTER_INPUT
  Button RESET (.out(RESET_out));
  assign controlled_buffer_1_out = EEPROM_data[9] ? eightbitregister_1_output_data : 8'bz;  // Controlled_Buffer controlled_buffer_1
  assign controlled_buffer_2_out = EEPROM_data[13] ? {4'b0000, eightbitregister_1_output_data[3:0]} : 8'bz;  // Controlled_Buffer controlled_buffer_2
  RAM #(.addrWidth(4), .clearpin("true"), .enables("line")) ram_1 (
    .addr(eightbitregister_2_output_direct), .clk(and_1_out), .dout(ram_1_dout), .clr(RESET_out));  // open: we, din
  EightBitRegister eightbitregister_1 (
    .INPUT_DATA(controlled_buffer_1_out), .ENABLE(EEPROM_data[9]), .OUT_ENABLE(EEPROM_data[10]),
    .CLK(and_1_out), .CLR(RESET_out), .OUTPUT_DIRECT(eightbitregister_1_output_direct),
    .OUTPUT_DATA(eightbitregister_1_output_data));
  LedBar ledbar_3 (
    .led0(eightbitregister_1_output_data[7]), .led1(eightbitregister_1_output_data[6]),
    .led2(eightbitregister_1_output_data[5]), .led3(eightbitregister_1_output_data[4]),
    .led4(eightbitregister_1_output_data[3]), .led5(eightbitregister_1_output_data[2]),
    .led6(eightbitregister_1_output_data[1]), .led7(eightbitregister_1_output_data[0]));
  EightBitRegister eightbitregister_2 (
    .INPUT_DATA(controlled_buffer_2_out), .ENABLE(EEPROM_data[13]), .OUT_ENABLE(EEPROM_data[12]),
    .CLK(and_1_out), .CLR(RESET_out),
    .OUTPUT_DIRECT({{4{eightbitregister_2_output_direct_2[7]}}, eightbitregister_2_output_direct}),
    .OUTPUT_DATA({{4{eightbitregister_2_output_direct_2[7]}}, eightbitregister_2_output_direct}));
  assign eightbitregister_1_output_data = EEPROM_data[11] ? ram_1_dout : 8'bz;  // Controlled_Buffer controlled_buffer_3
  assign controlled_buffer_4_out = EEPROM_data[6] ? eightbitregister_1_output_data : 8'bz;  // Controlled_Buffer controlled_buffer_4
  assign controlled_buffer_5_out = EEPROM_data[4] ? eightbitregister_1_output_data : 8'bz;  // Controlled_Buffer controlled_buffer_5
  assign controlled_buffer_6_out = EEPROM_data[2] ? eightbitregister_1_output_data : 8'bz;  // Controlled_Buffer controlled_buffer_6
  ProgramCounter programcounter_2 (
    .OUT_ENABLE(EEPROM_data[8]), .LOAD_ENABLE(EEPROM_data[0]), .CLR(RESET_out), .cin(1'b1),
    .enable(EEPROM_data[7]), .CLK(and_1_out), .COUNTER_INPUT(eightbitregister_1_output_data[3:0]),
    .out_to_bus(eightbitregister_1_output_data));
  LedBar #(.matrixcols(18)) ledbar_4 (
    .led0(EEPROM_data[14]), .led1(EEPROM_data[13]), .led2(EEPROM_data[12]), .led3(EEPROM_data[11]),
    .led4(EEPROM_data[10]), .led5(EEPROM_data[9]), .led6(EEPROM_data[8]), .led7(EEPROM_data[7]),
    .led8(EEPROM_data[6]), .led9(EEPROM_data[5]), .led10(EEPROM_data[4]), .led11(EEPROM_data[3]),
    .led12(EEPROM_data[2]), .led13(EEPROM_data[1]), .led14(EEPROM_data[0]), .led15(EEPROM_data[15]),
    .led16(EEPROM_data[16]), .led17(EEPROM_data[17]));
  EightBitRegister eightbitregister_3 (
    .INPUT_DATA(controlled_buffer_4_out), .ENABLE(EEPROM_data[6]), .OUT_ENABLE(EEPROM_data[5]),
    .CLK(and_1_out), .CLR(RESET_out), .OUTPUT_DIRECT(eightbitregister_3_output_direct),
    .OUTPUT_DATA(eightbitregister_1_output_data));
  EightBitRegister eightbitregister_4 (
    .INPUT_DATA(controlled_buffer_5_out), .ENABLE(EEPROM_data[4]), .OUT_ENABLE(EEPROM_data[3]),
    .CLK(and_1_out), .CLR(RESET_out), .OUTPUT_DIRECT(eightbitregister_4_output_direct),
    .OUTPUT_DATA(eightbitregister_1_output_data));
  EightBitRegister eightbitregister_5 (
    .INPUT_DATA(controlled_buffer_6_out), .ENABLE(EEPROM_data[2]), .OUT_ENABLE(EEPROM_data[1]),
    .CLK(and_1_out), .CLR(RESET_out), .OUTPUT_DIRECT(eightbitregister_5_output_direct),
    .OUTPUT_DATA(eightbitregister_1_output_data));
  Controlled_Buffer #(.width(8)) controlled_buffer_7 (
    .in(eightbitregister_1_output_data), .en(EEPROM_data[1]));  // open: out
  Hex_Digit_Display hex_digit_display_1 (.value(binary_to_bcd_converter_1_p3));  // open: dp
  // Binary_to_BCD_converter #(.binvalue(8)) binary_to_bcd_converter_1: pin names not known; wires that end beside it: RESET_out, eightbitregister_5_output_direct, binary_to_bcd_converter_1_p3, binary_to_bcd_converter_1_p4, binary_to_bcd_converter_1_p5
  Hex_Digit_Display hex_digit_display_2 (.value(binary_to_bcd_converter_1_p4));  // open: dp
  ALU alu_1 (
    .SUB(EEPROM_data[16]), .CLK(and_1_out), .ENABLE(EEPROM_data[15]), .CLR(RESET_out),
    .A_IN(eightbitregister_3_output_direct), .OUT_ENABLE(EEPROM_data[17]),
    .B_IN(eightbitregister_4_output_direct), .OUT_DATA(eightbitregister_1_output_data));  // open: CO
  Hex_Digit_Display hex_digit_display_3 (.value(binary_to_bcd_converter_1_p5));  // open: dp
  // also tied to GND on the sheet: eightbitregister_2_output_direct_2[7]

  // Notes on the sheet:
  //   contents of EEPROM (hex, n*v repeats v):
  //   2100 a80 14*0 2100 a80 2400 840 12*0 2100 a80 2400 810 8000 20040 10*0 2100 a80 2400 801 172*0 2100
  //   a80 24
  //   CLOCK
  //   HALT
  //   MAR
  //   Instruction Register
  //   BUS
  //   HLT
  //   MI
  //   RO
  //   MO
  //   IO
  //   II
  //   PCO
  //   A Register
  //   B Register
  //   Out Register
  //   Control Logic
  //   PCE
  //   AI
  //   ADD_O
  //   SUB
  //   BI
  //   AO
  //   BO
  //   ALU_O
  //   OI
  //   OO
  //   PCLE
endmodule

module ProgramCounter (
  input  OUT_ENABLE,
  input  LOAD_ENABLE,
  input  CLR,
  input  cin,
  input  enable,
  input  CLK,
  input  [3:0] COUNTER_INPUT,
  output [7:0] out_to_bus
);

  wire [3:0] counter_1_q;

  Counter #(.max('hf), .width(4)) counter_1 (
    .clr(CLR), .load(LOAD_ENABLE), .up(cin), .count(enable), .clk(CLK), .D(COUNTER_INPUT), .Q(counter_1_q));  // open: carry
  assign out_to_bus = OUT_ENABLE ? {4'b0000, counter_1_q} : 8'bz;  // Controlled_Buffer controlled_buffer_1
endmodule

module MAR (
  input  OUT_EN,
  input  EN,
  input  [3:0] from_bus,
  input  CLR,
  input  CLK,
  output [3:0] bus_out
);

  wire and_1_out, d_ff_1_q, d_ff_2_q, d_ff_3_q, d_ff_4_q;
  wire [3:0] controlled_buffer_1_out, controlled_buffer_2_out;

  and and_1 (and_1_out, 1'b1, OUT_EN);
  assign controlled_buffer_1_out = EN ? from_bus : 4'bz;  // Controlled_Buffer controlled_buffer_1
  D_Flip_Flop d_ff_1 (.D(controlled_buffer_1_out[0]), .clk(CLK), .Q(d_ff_1_q), .reset(CLR));  // open: Qn, preset
  D_Flip_Flop d_ff_2 (.D(controlled_buffer_1_out[1]), .clk(CLK), .Q(d_ff_2_q), .reset(CLR));  // open: Qn, preset
  D_Flip_Flop d_ff_3 (.D(controlled_buffer_1_out[2]), .clk(CLK), .Q(d_ff_3_q), .reset(CLR));  // open: Qn, preset
  D_Flip_Flop d_ff_4 (.D(controlled_buffer_1_out[3]), .clk(CLK), .Q(d_ff_4_q), .reset(CLR));  // open: Qn, preset
  assign controlled_buffer_2_out[0] = and_1_out ? d_ff_1_q : 1'bz;  // Controlled_Buffer controlled_buffer_2
  assign controlled_buffer_2_out[1] = and_1_out ? d_ff_2_q : 1'bz;  // Controlled_Buffer controlled_buffer_3
  assign controlled_buffer_2_out[2] = and_1_out ? d_ff_3_q : 1'bz;  // Controlled_Buffer controlled_buffer_4
  assign controlled_buffer_2_out[3] = and_1_out ? d_ff_4_q : 1'bz;  // Controlled_Buffer controlled_buffer_5
endmodule

module EightBitRegister (
  input  [7:0] INPUT_DATA,
  input  ENABLE,
  input  OUT_ENABLE,
  input  CLK,
  input  CLR,
  output [7:0] OUTPUT_DIRECT,
  output [7:0] OUTPUT_DATA
);

  Register register_1 (.D(INPUT_DATA), .en(ENABLE), .clk(CLK), .Q(OUTPUT_DIRECT), .clr(CLR));
  assign OUTPUT_DATA = OUT_ENABLE ? OUTPUT_DIRECT : 8'bz;  // Controlled_Buffer controlled_buffer_1
endmodule

module ALU (
  input  SUB,
  input  CLK,
  input  ENABLE,
  input  CLR,
  input  [7:0] A_IN,
  input  OUT_ENABLE,
  input  [7:0] B_IN,
  output [7:0] OUT_DATA,
  output CO
);

  wire and_1_out, and_2_out, and_3_out, and_4_out, and_5_out, and_6_out, and_7_out, and_8_out, and_9_out,
       and_10_out, and_11_out, and_12_out, and_13_out, and_14_out, and_15_out, and_16_out, or_1_out,
       or_2_out, or_3_out, or_4_out, or_5_out, or_6_out, or_7_out, xor_1_out, xor_2_out, xor_3_out,
       xor_4_out, xor_5_out, xor_6_out, xor_7_out, xor_8_out, xor_9_out, xor_10_out, xor_11_out, xor_12_out,
       xor_13_out, xor_14_out, xor_15_out, xor_16_out;
  wire [7:0] xor_17_out;

  xor xor_1 (xor_1_out, B_IN[0], SUB);
  xor xor_2 (xor_2_out, B_IN[1], SUB);
  xor xor_3 (xor_3_out, B_IN[2], SUB);
  xor xor_4 (xor_4_out, B_IN[3], SUB);
  xor xor_5 (xor_5_out, B_IN[4], SUB);
  xor xor_6 (xor_6_out, B_IN[5], SUB);
  xor xor_7 (xor_7_out, B_IN[6], SUB);
  xor xor_8 (xor_8_out, B_IN[7], SUB);
  xor xor_9 (xor_9_out, A_IN[0], xor_1_out);
  and and_1 (and_1_out, xor_1_out, A_IN[0]);
  xor xor_10 (xor_10_out, A_IN[1], xor_2_out);
  and and_2 (and_2_out, xor_2_out, A_IN[1]);
  xor xor_11 (xor_11_out, A_IN[2], xor_3_out);
  and and_3 (and_3_out, xor_3_out, A_IN[2]);
  xor xor_12 (xor_12_out, A_IN[3], xor_4_out);
  and and_4 (and_4_out, xor_4_out, A_IN[3]);
  xor xor_13 (xor_13_out, A_IN[4], xor_5_out);
  and and_5 (and_5_out, xor_5_out, A_IN[4]);
  xor xor_14 (xor_14_out, A_IN[5], xor_6_out);
  and and_6 (and_6_out, xor_6_out, A_IN[5]);
  xor xor_15 (xor_15_out, A_IN[6], xor_7_out);
  and and_7 (and_7_out, xor_7_out, A_IN[6]);
  xor xor_16 (xor_16_out, A_IN[7], xor_8_out);
  and and_8 (and_8_out, xor_8_out, A_IN[7]);
  and and_9 (and_9_out, xor_9_out, SUB);
  and and_10 (and_10_out, xor_10_out, or_1_out);
  and and_11 (and_11_out, xor_11_out, or_2_out);
  and and_12 (and_12_out, xor_12_out, or_3_out);
  and and_13 (and_13_out, xor_13_out, or_4_out);
  and and_14 (and_14_out, xor_14_out, or_5_out);
  and and_15 (and_15_out, xor_15_out, or_6_out);
  and and_16 (and_16_out, xor_16_out, or_7_out);
  xor xor_17 (xor_17_out[0], xor_9_out, SUB);
  or or_1 (or_1_out, and_9_out, and_1_out);
  xor xor_18 (xor_17_out[1], xor_10_out, or_1_out);
  or or_2 (or_2_out, and_10_out, and_2_out);
  xor xor_19 (xor_17_out[2], xor_11_out, or_2_out);
  or or_3 (or_3_out, and_11_out, and_3_out);
  xor xor_20 (xor_17_out[3], xor_12_out, or_3_out);
  or or_4 (or_4_out, and_12_out, and_4_out);
  xor xor_21 (xor_17_out[4], xor_13_out, or_4_out);
  or or_5 (or_5_out, and_13_out, and_5_out);
  xor xor_22 (xor_17_out[5], xor_14_out, or_5_out);
  or or_6 (or_6_out, and_14_out, and_6_out);
  xor xor_23 (xor_17_out[6], xor_15_out, or_6_out);
  or or_7 (or_7_out, and_15_out, and_7_out);
  xor xor_24 (xor_17_out[7], xor_16_out, or_7_out);
  or or_8 (CO, and_16_out, and_8_out);
  EightBitRegister eightbitregister_1 (
    .INPUT_DATA(xor_17_out), .ENABLE(ENABLE), .OUT_ENABLE(OUT_ENABLE), .CLK(CLK), .CLR(CLR),
    .OUTPUT_DATA(OUT_DATA));  // open: OUTPUT_DIRECT

  // Notes on the sheet:
  //   A
  //   B
  //   A
  //   B
  //   A
  //   B
  //   A
  //   B
  //   A
  //   B
  //   A
  //   B
  //   A
  //   B
  //   A
  //   B
  //   Carry Out/Overflow
endmodule
